// Logisim project new_CPU.circ as structural Verilog: 4 circuits, main circuit main
module main (
  input  [3:0] B,
  input  [3:0] A,
  input  [3:0] command
);

  ROM #(.dataWidth(12)) rom_1 (.data({command, A, B}));  // open: addr
  MyALU myalu_1 ();  // open: Cin, in_2, in_3, in_4, M, out_6, A_B, Sign
  ROM #(.addrWidth(4), .dataWidth(4)) rom_2 ();  // open: addr, data
endmodule

module MyALU (
  input  Cin,
  input  [3:0] in_2,
  input  [3:0] in_3,
  input  [3:0] in_4,
  input  M,
  output [3:0] out_6,
  output A_B,
  output Sign
);

  wire n74181_1_p13, n74181_1_p14, n74181_1_p16, n74181_1_p18, not_2_out;

  // _74181 74181_1: pin names not known; wires that end beside it: in_4[0], in_3[1], in_3[0], in_4[1], in_2[3], in_3[2], in_2[2], in_4[2], in_2[1], in_3[3], in_2[0], in_4[3], n74181_1_p13, n74181_1_p14, M, n74181_1_p16, out_6[0], n74181_1_p18, out_6[1], A_B, out_6[2], out_6[3]
  and and_1 (Sign, n74181_1_p14, not_2_out);
  not not_1 (n74181_1_p13, Cin);
  not not_2 (not_2_out, A_B);

  // Notes on the sheet:
  //   Op
  //   A_in
  //   B_in
  //   Output
  //   Cout
  //   Pn
endmodule

module PC (
  input  in_1,
  input  ClockWait,
  output [7:0] CA,
  output [3:0] Operation,
  output [3:0] A,
  output [3:0] B
);

  wire ClockUpd, not_1_out;
  wire [7:0] controlled_buffer_1_out, counter_1_q;

  Counter #(.ongoal("stay")) counter_1 (.clk(ClockUpd), .D(CA), .Q(counter_1_q));  // open: clr, load, up, count, carry
  assign controlled_buffer_1_out = not_1_out ? counter_1_q : 8'bz;  // Controlled_Buffer controlled_buffer_1
  ROM #(.dataWidth(12)) rom_1 (.addr(controlled_buffer_1_out), .data({B, A, Operation}));
  not not_1 (not_1_out, ClockWait);
  and and_1 (ClockUpd, not_1_out, in_1);

  // Other names for the same wires on the sheet: Clock = in_1; CurrAdress[7:0] = CA

  // Notes on the sheet:
  //   contents of rom_1 (hex, n*v repeats v):
  //   0 151 144 a45
endmodule

module OperationDecoder (
  input  [3:0] Operation,
  output out_2,
  output out_3,
  output out_4,
  output out_5,
  output out_6,
  output out_7,
  output out_8
);

  wire Jump;
  wire [15:7] rom_1_data;

  ROM #(.addrWidth(4), .dataWidth(16)) rom_1 (
    .addr(Operation), .data({rom_1_data, out_8, out_7, out_6, out_5, out_4, Jump, out_2}));

  assign out_3 = out_2;

  // Other names for the same wires on the sheet: Digit = out_2; ALULogic = out_4; ALU = out_5; ALUCarry = out_6;
  //   FlagWrite = out_7; Adress = out_8

  // Notes on the sheet:
  //   contents of rom_1 (hex, n*v repeats v):
  //   0 1 41 40 c 0 38 0 0 8 0 0 4*2
endmodule
